# Fritzing sketch LCDTest (saved by Fritzing 0.9.2b)
breadboards: 1

parts:
  LCD1 = LCD screen
  Part1 = Arduino Mega 2560 (Rev3)
  R1 = Resistor [tolerance=±5% resistance=220 package=THT]
  U1 = POT [package=alps_pot]

nets:
  VSS: LCD1.VSS, LCD1.R/W, LCD1.LED-, Part1.GND, U1.E
  N1: LCD1.V0, U1.S
  N2: LCD1.RS, Part1.D8_PWM
  N3: LCD1.E, Part1.D9_PWM
  N4: LCD1.DB4, Part1.D10_PWM
  N5: LCD1.DB5, Part1.D11_PWM
  N6: LCD1.DB6, Part1.D12_PWM
  N7: LCD1.DB7, Part1.D13_PWM
  N8: LCD1.LED+, R1.Pin_0
  N9: Part1.5V, R1.Pin_1, U1.A
